# Fritzing sketch diagram (saved by Fritzing 0.9.10b)

parts:
  microSD1 = MicroSD Card Module
  Part3 = Solid State High Level Relay Module [package=relay]
  Part4 = Passive Buzzer
  Grove1 = Grove 3 Axis Digital Accelerometer 16g
  J1 = female pin header, 2 pins [form="♀ (female)"]
  J2 = female pin header, 2 pins [form="♀ (female)"]
  J3 = female pin header, 2 pins [form="♀ (female)"]
  J4 = female pin header, 2 pins [form="♀ (female)"]
  Part10 = Arduino Uno (Rev3)
  Part11 = Arduino Mega ADK (Rev3)
  Part12 = Solid State High Level Relay Module [package=relay]
  Part13 = Passive Buzzer
  J5 = female pin header, 2 pins [form="♀ (female)"]
  J6 = female pin header, 2 pins [form="♀ (female)"]
  A1 = j5019
  U1 = LIPO-1000mAh [package=lipo-1000]
  J7 = female pin header, 2 pins [form="♀ (female)"]
  Grove2 = Grove 3 Axis Digital Accelerometer 16g
  A2 = j5019
  U2 = LIPO-1000mAh [package=lipo-1000]
  ZS-042_RTC1 = ZS-042 RTC Module
  J8 = female pin header, 2 pins [form="♀ (female)"]

nets:
  N1: microSD1.GND, J1.pin1
  N2: microSD1.VCC, J1.pin2
  N3: microSD1.MISO, Part11.D50/MISO
  N4: microSD1.MOSI, Part11.D51/MOSI
  N5: microSD1.SCK, Part11.D52/SCK
  N6: microSD1.CS, Part11.D53/SS
  N7: Part3.DC+, J3.pin2
  N8: Part3.CH1, Part10.D11_PWM/MOSI
  N9: Part3.DC-, J3.pin1
  N10: Part4.GND, J4.pin2
  N11: Part4.S, Part10.D12/MISO
  N12: Part4.NC, J4.pin1
  N13: Grove1.GND, J2.pin1
  N14: Grove1.VCC, J2.pin2
  N15: Grove1.SDA, Part10.A4/SDA
  N16: Grove1.SCL, Part10.A5/SCL
  N17: Part10.GND, A1.Pin_2, A1.Pin_5, U1.-
  N18: Part10.VIN, A1.Pin_1
  N19: Part11.D21/SCL, Grove2.SCL, ZS-042_RTC1.SCL
  N20: Part11.D20/SDA, Grove2.SDA, ZS-042_RTC1.SDA
  N21: Part11.D12_PWM, Part13.S
  N22: Part11.D11_PWM, Part12.CH1
  N23: Part11.GND, A2.Pin_2, A2.Pin_5, U2.-
  N24: Part11.VIN, A2.Pin_1
  N25: Part12.DC+, J6.pin2
  N26: Part12.DC-, J6.pin1
  N27: Part13.GND, J5.pin2
  N28: Part13.NC, J5.pin1
  N29: A1.Pin_6, U1.+
  N30: J7.pin1, Grove2.GND
  N31: J7.pin2, Grove2.VCC
  N32: A2.Pin_6, U2.+
  N33: ZS-042_RTC1.GND, J8.pin1
  N34: ZS-042_RTC1.VCC, J8.pin2

custom parts:
  Solid State High Level Relay Module: 5V Omron solid state relay 240V 2A output with resistance fuse.
  j5019: This module is a small single cell lithium battery charging module which also includes a 1A step-up (boost) converter for powering a large range of applications.
